# Fritzing sketch scheme (saved by Fritzing 0.9.3b)
breadboards: 1

parts:
  J1 = T Cobbler Plus
  LCD1 = LCD screen
  S2 = Momentary Switch [package=ksa_sealed_tac_switch]
  S3 = Momentary Switch [package=ksa_sealed_tac_switch]
  S4 = Momentary Switch [package=ksa_sealed_tac_switch]
  S5 = Momentary Switch [package=ksa_sealed_tac_switch]
  Raspberry_Pi_2 = Raspberry Pi 4 [part_number=RPI-4-b]
  U1 = WS2812 RGB LED strip
  JACK1 = 2.1mm DC Barrel Jack

nets:
  N1: J1.#17, S3.1, S3.2
  N2: J1.#18, U1.DIN
  N3: J1.#27, LCD1.E
  N4: J1.#22, LCD1.RS
  N5: J1.#6, LCD1.DB4
  N6: J1.#13, LCD1.DB5
  N7: J1.#19, LCD1.DB6
  N8: J1.#16, S5.1, S5.2
  N9: J1.#26, LCD1.DB7
  N10: J1.#20, S2.2
  N11: J1.#21, S4.2
  3V3: J1.3.3V#41, J1.3.3V#57, Raspberry_Pi_2.3v3, Raspberry_Pi_2.3V3
  5V: J1.5V, Raspberry_Pi_2.5V
  N12: J1.GPIO_2, Raspberry_Pi_2.GPIO2
  N13: J1.GPIO_3, Raspberry_Pi_2.GPIO3
  N14: J1.GND#46, J1.GND#49, J1.GND#54, J1.GND#60, J1.GND#65, J1.GND#70, J1.GND#74, J1.GND#79, Raspberry_Pi_2.GND
  N15: J1.GPIO_4, Raspberry_Pi_2.GPIO4
  N16: J1.GPIO_14, Raspberry_Pi_2.GPIO14
  N17: J1.GPIO_15, Raspberry_Pi_2.GPIO15
  N18: J1.GPIO_17, Raspberry_Pi_2.GPIO17
  N19: J1.GPIO_18, Raspberry_Pi_2.GPIO18
  N20: J1.GPIO_27, Raspberry_Pi_2.GPIO27
  N21: J1.GPIO_22, Raspberry_Pi_2.GPIO22
  N22: J1.GPIO_23, Raspberry_Pi_2.GPIO23
  N23: J1.GPIO_24, Raspberry_Pi_2.GPIO24
  N24: J1.GPIO_10, Raspberry_Pi_2.GPIO10
  N25: J1.GPIO_9, Raspberry_Pi_2.GPIO9
  N26: J1.GPIO_25, Raspberry_Pi_2.GPIO25
  N27: J1.GPIO_11, Raspberry_Pi_2.GPIO11
  N28: J1.GPIO_8, Raspberry_Pi_2.GPIO8
  N29: J1.GPIO_7, Raspberry_Pi_2.GPIO7
  N30: J1.ID_SD, Raspberry_Pi_2.ID_SD
  N31: J1.ID_SC, Raspberry_Pi_2.ID_SC
  N32: J1.GPIO_5, Raspberry_Pi_2.GPIO5
  N33: J1.GPIO_6, Raspberry_Pi_2.GPIO6
  N34: J1.GPIO_12, Raspberry_Pi_2.GPIO12
  N35: J1.GPIO_13, Raspberry_Pi_2.GPIO13
  N36: J1.GPIO_19, Raspberry_Pi_2.GPIO19
  N37: J1.GPIO_16, Raspberry_Pi_2.GPIO16
  N38: J1.GPIO_26, Raspberry_Pi_2.GPIO26
  N39: J1.GPIO_20, Raspberry_Pi_2.GPIO20
  N40: J1.GPIO_21, Raspberry_Pi_2.GPIO21
  VSS: LCD1.VSS, LCD1.V0, LCD1.R/W, LCD1.LED-, S2.4, S3.3, S3.4, S4.4, S5.3, S5.4, U1.GND, JACK1.switch
  VDD: LCD1.VDD, LCD1.LED+, U1.VCC, JACK1.center

notes:
  LCD
  RS(Register Select) GPIO 22
  E(Enable) GPIO 27
  D4(Data 4) GPIO 6
  D5(Data 5) GPIO 13
  D6(Data 6) GPIO 19
  D7(Data 7) GPIO 26
  Buttons
  Up GPIO 17
  Down GPIO 16
  Left GPIO 20
  Right GPIO 21
  LED Strip
  Data GPIO 18

custom parts:
  T Cobbler Plus: The T-Cobbler Plus is an add on prototyping board from Adafruit specifically designed for the Raspberry Pi B+ that can break out all those tasty power, GPIO, I2C and SPI pins from the 40-pin header onto a solderless breadboard. This set will make "cobbling together" prototypes with the Pi super easy. The T-Cobbler Plus can plug into any solderless breadboard.
  Raspberry Pi 4: The RPi4, a faster version of the awesome Raspberry Pi 2 B ARM Board with 40 pin gpio. Ready for special Raspberry Pi B+ and RPi2 Hat (Hardware attached (on) top)
  WS2812 RGB LED strip: WS2812 strip
  2.1mm DC Barrel Jack: 2.1mm DC Barrel Jack with Thru-Hole Connectors (breadboardable)
